# Fritzing sketch Prise_Connecte (saved by Fritzing 0.9.2b)

parts:
  HLK-PM1 = HLK-PM01
  U1 = 2-Channel 5v Relay Shield [package=relay-2ch5v10a]
  U2 = 2-Channel 5v Relay Shield [package=relay-2ch5v10a]
  U6 = Power Outlet [chip_label=IC package="SIP (Single Inline) [THT]"]
  U7 = Power Outlet [chip_label=IC package="SIP (Single Inline) [THT]"]
  ESP8266-1 = ESP8266-12 [part_number=ESP8266-12]
  S1 = Pushbutton [package="[THT]"]
  U8 = SWITCH-SPST-2 [package=switch-spst-vertical]
  JP1 = Header 2 [package=jst-2-smd]
  Composant1 = DC-DC Power Module (3.3v)
  JP4 = Header 2 [package=jst-2-pth]
  Composant2 = ws2812b [package=THT]
  JP5 = Header 10 [package=1x10-2mm-smd]
  JP3 = Header 10 [package=1x10-2mm-smd]
  R1 = Resistor [tolerance=±5% resistance=10k package=THT]
  R2 = Resistor [tolerance=±5% resistance=10k package=THT]
  R3 = Resistor [tolerance=±5% resistance=10k package=THT]
  R4 = Resistor [tolerance=±5% resistance=10k package=THT]
  R5 = Resistor [tolerance=±5% resistance=10k package=THT]
  IC1 = ULN2003A [package="SO16 [SMD]"]
  Q1 = Temperature sensor [package="TO92 [THT]"]
  R6 = Resistor [tolerance=±5% resistance=220 package=THT]
  JP6 = Header 4 [package=molex-1x4_lock]
  S2 = SPST Switch [package=switch-spdt_lock.007s]

nets:
  N1: HLK-PM1.AC#0, U6.neutral1, U6.neutral2, U7.neutral1, U7.neutral2
  N2: HLK-PM1.AC#1, U1.K1-Off, U1.K2-Off, U2.K1-Off, U2.K2-Off, U8.O
  N3: HLK-PM1.-Vo, JP1.2
  N4: HLK-PM1.+Vo, JP1.1
  VCC: U1.VCC, U2.VCC, JP5.10
  GND: U1.GND, U2.GND, JP5.5
  N5: U1.IN1, JP5.6
  N6: U1.IN2, JP5.7
  N7: U1.K1-On, U6.hot2
  N8: U1.K2-On, U6.hot1
  N9: U2.IN1, JP5.8
  N10: U2.IN2, JP5.9
  N11: U2.K1-On, U7.hot2
  N12: U2.K2-On, U7.hot1
  N13: U6.ground, U7.ground
  N14: ESP8266-1.REST, S1.Pin_4, R5.Pin_1
  N15: ESP8266-1.CH_PD, R4.Pin_1
  N16: ESP8266-1.GPIO14, IC1.In_5
  N17: ESP8266-1.GPIO13, Composant2.DOUT
  VCC_2: ESP8266-1.VCC, Composant1.Vin, JP3.4, R1.Pin_1, R2.Pin_1, R4.Pin_0, R5.Pin_0, Q1.Vdd, R6.Pin_0
  N18: ESP8266-1.TXD, IC1.In_1
  N19: ESP8266-1.RXD, IC1.In_2
  N20: ESP8266-1.GPIO4, IC1.In_4
  N21: ESP8266-1.GPIO5, Q1.DQ
  N22: ESP8266-1.GPIO0, R2.Pin_0, S2.P
  N23: ESP8266-1.GPIO2, R1.Pin_0, IC1.In_6
  N24: ESP8266-1.GPIO15, R3.Pin_0, IC1.In_7
  GND_2: ESP8266-1.GND, S1.Pin_1, S1.Pin_2, Composant1.GND, JP3.1, JP3.5, R3.Pin_1, IC1.0V, Q1.GND, R6.Pin_1, S2.S
  N25: Composant1.Vout, JP4.2, Composant2.VSS, JP3.10, IC1.COM_-_Common
  N26: Composant1.GND*, JP4.1, Composant2.VDD
  N27: JP5.1, JP6.1
  N28: JP5.2, JP6.2
  N29: JP5.3, JP6.3
  N30: JP5.4, JP6.4
  N31: JP3.2, IC1.Out_1
  N32: JP3.3, IC1.Out_2
  N33: JP3.6, IC1.Out_4
  N34: JP3.7, IC1.Out_5
  N35: JP3.8, IC1.Out_6
  N36: JP3.9, IC1.Out_7

custom parts:
  2-Channel 5v Relay Shield: 2 Channel 5v Relay Shield w. 2x SPD-06VDC-SD-C
  Power Outlet: A standard power outlet. Silver screws are neutral, brass screws are hot. Green screw is ground.
  DC-DC Power Module (3.3v): DC-DC Power Module based con AMS1117-3.3 Input: DC 4.5~7V (input power must higher 1V than output power); Output: 3.3V (+/-0.05V error), 800mA
  Temperature sensor: Dellas temperature sensor
